# Fritzing sketch Solenoid (saved by Fritzing 0.9.3b)
breadboards: 1

parts:
  Vo_Atmega128 = Resistor [tolerance=±5% resistance=1k package="0603 [SMD]"]
  Vo = male pin header, 1 pin [form="♂ (male)"]
  D1 = Rectifier Diode [package="Melf DO-213 AA [SMD]"]
  Q1 = TRANSISTOR_NPN [package=to-92]
  Opamp = IC, DIP package, 8 pins [chip_label=IC]
  R1 = Resistor [tolerance=±5% resistance=1k package=THT]
  Relay = IC, DIP package, 8 pins [chip_label=Relay]
  12V_in = male pin header, 1 pin [form="♂ (male)"]
  Solenoid = male pin header, 1 pin [form="♂ (male)"]
  IR = smd LED [color="Red (660nm)" package="1206 [SMD]"]
  IR_recv = smd LED [color="Infrared (940nm)" package="1206 [SMD]"]
  R2 = Resistor [tolerance=±5% resistance=1k package=THT]
  Out = male pin header, 1 pin [form="♂ (male)"]

nets:
  N1: Vo_Atmega128.Pin_0, Q1.B
  N2: Vo_Atmega128.Pin_1, Vo.pin1
  N3: D1.cathode, Q1.E, Relay.pin5
  GND: D1.anode, Opamp.pin4, R1.Pin_0, Relay.pin4, R2.Pin_1
  5V: Q1.C, Opamp.pin8, IR.anode, IR_recv.cathode
  N4: Opamp.pin5, R1.Pin_1, IR_recv.anode
  N5: Opamp.pin6, Opamp.pin7, Out.pin1
  N6: Relay.pin1, Solenoid.pin1
  N7: Relay.pin3, 12V_in.pin1
  N8: IR.cathode, R2.Pin_0

notes:
  5V
  12V
  Solenoid, This is the circuit to control the solenoid and the motor., 1
  Gnd
  Solenoid
