# Fritzing sketch breadboard (saved by Fritzing 0.9.3b)
breadboards: 4

parts:
  Microcontroller = IC, DIP package, 40 pins [chip_label="Atmega 162"]
  RESET = Pushbutton [package="[SMD]"]
  LED = LED - 3mm [color="Red (633nm)" package="3 mm [THT]"]
  Voltage_regulator_NCP = Capacitor [package=cap-pth-small]
  U1 = Voltage Regulator - 5V [package="TO220 [THT]"]
  Clock_Atmega = Crystal [frequency="4 MHz" package=THT]
  RS232 = IC, DIP package, 20 pins [chip_label=MAX233]
  UART_connector = male pin header, 5 pins [form="♂ (male)"]
  CAN_controller = IC, DIP package, 18 pins [chip_label=MCP2515]
  Atmega = Capacitor [package=cap-pth-large]
  CAN_trancv = IC, DIP package, 8 pins [chip_label=MC2551]
  Latch = IC, DIP package, 20 pins [chip_label=SN74ALS573C]
  ADC = DIP - 20 pins [chip_label=ADC0844CCN package="DIP (Dual Inline) [THT]"]
  SRAM = IC, DIP package, 28 pins [chip_label="SRAM IDT_7164SL"]
  GAL = IC, DIP package, 20 pins [chip_label=GAL16V8D]
  GAL_NCP = Ceramic Capacitor [capacitance="100 nF" package="0603 [SMD, multilayer]"]
  JTAG = male pin header, 4 pins [form="♂ (male)"]
  Latch_NCP = Capacitor [package=cap-pth-large]
  Game_board = male pin header, 16 pins [form="♂ (male)"]
  Game_board_buttons = male pin header, 3 pins [form="♂ (male)"]
  ADC_NCP = Capacitor [package=cap-pth-large]
  OSC2_2 = Capacitor [package=cap-pth-small2]
  Clock_CAN = Crystal [frequency="16 MHz" package=THT]
  OSC2_1 = Capacitor [package=cap-pth-large]
  Terminate_CAN = Resistor [tolerance=±5% resistance=120 package="0402 [SMD]"]
  CAN_bus = male pin header, 2 pins [form="♂ (male)"]
  CAN = Capacitor [package=cap-pth-large]
  Reset_CAN = Resistor [tolerance=±5% resistance=22k package="0402 [SMD]"]
  VCC1 = Battery block 9V
  Reset_Atmega = Resistor [tolerance=±5% resistance=22k package="0402 [SMD]"]
  OSC1_2 = Capacitor [package=cap-pth-large]
  OSC1_1 = Capacitor [package=cap-pth-small2]
  Reset = Capacitor [package=cap-pth-large]
  Jtag_Pow = male pin header, 2 pins [form="♂ (male)"]
  RS_resistor = Resistor [tolerance=±5% resistance=22k package="0402 [SMD]"]
  JTAG_Power = male pin header, 1 pin [form="♂ (male)"]
  SRAM_2 = Ceramic Capacitor [capacitance="100 nF" package="0603 [SMD, multilayer]"]

nets (from the breadboard view):
  N1: Microcontroller.pin1, LED.anode
  N2: Microcontroller.pin2, Game_board_buttons.pin3
  N3: Microcontroller.pin3, Game_board_buttons.pin2
  N4: Microcontroller.pin4, Game_board_buttons.pin1
  N5: Microcontroller.pin5, CAN_controller.pin16
  N6: Microcontroller.pin6, CAN_controller.pin14
  N7: Microcontroller.pin7, CAN_controller.pin15
  N8: Microcontroller.pin8, CAN_controller.pin13
  N9: Microcontroller.pin9, RESET.Pin_1, RESET.Pin_2, CAN_controller.pin17, Reset_CAN.Pin_1, Reset_Atmega.Pin_1, Reset.1
  N10: Microcontroller.pin10, RS232.pin3
  N11: Microcontroller.pin11, RS232.pin2
  N12: Microcontroller.pin16, ADC.!WR, SRAM.pin27, Game_board.pin7
  N13: Microcontroller.pin17, ADC.!RD, SRAM.pin22, OSC1_1.2
  N14: Microcontroller.pin18, Clock_Atmega.pin_1
  N15: Microcontroller.pin19, Clock_Atmega.pin_0, OSC1_2.2, OSC1_1.1
  N16: Microcontroller.pin20, RESET.Pin_3, RESET.Pin_4, LED.cathode, Voltage_regulator_NCP.2, U1.GND, RS232.pin6, Atmega.2, CAN_trancv.pin2, Latch.pin1, Latch.pin10, ADC.AGND, ADC.DGND, SRAM.pin2, SRAM.pin14, GAL.pin10, GAL_NCP.0, Latch_NCP.2, Game_board.pin16, ADC_NCP.1, CAN.1, OSC1_2.1, Reset.2, Jtag_Pow.pin1, Jtag_Pow.pin2, RS_resistor.Pin_0
  N17: Microcontroller.pin21, SRAM.pin23, GAL.pin4
  N18: Microcontroller.pin22, SRAM.pin21, GAL.pin3
  N19: Microcontroller.pin23, SRAM.pin24, GAL.pin2
  N20: Microcontroller.pin24, SRAM.pin25, GAL.pin1
  N21: Microcontroller.pin25, JTAG.pin1
  N22: Microcontroller.pin26, JTAG.pin2
  N23: Microcontroller.pin27, JTAG.pin3
  N24: Microcontroller.pin28, JTAG.pin4
  N25: Microcontroller.pin30, Latch.pin11
  N26: Microcontroller.pin32, Latch.pin9, ADC.DB7, SRAM.pin19, Game_board.pin15
  N27: Microcontroller.pin33, Latch.pin8, ADC.DB6, SRAM.pin18, Game_board.pin14
  N28: Microcontroller.pin34, Latch.pin7, ADC.DB5, SRAM.pin17, Game_board.pin13
  N29: Microcontroller.pin35, Latch.pin6, ADC.DB4, SRAM.pin16, Game_board.pin12
  N30: Microcontroller.pin36, Latch.pin5, ADC.DB3, SRAM.pin15, Game_board.pin11
  N31: Microcontroller.pin37, Latch.pin4, ADC.DB2, SRAM.pin13, Game_board.pin10
  N32: Microcontroller.pin38, Latch.pin3, ADC.DB1, SRAM.pin12, Game_board.pin9
  N33: Microcontroller.pin39, Latch.pin2, ADC.DB0, SRAM.pin11, Game_board.pin8
  N34: Microcontroller.pin40, Atmega.1
  N35: Voltage_regulator_NCP.1, U1.input_voltage
  N36: U1.output_voltage, RS232.pin7, CAN_controller.pin18, CAN_trancv.pin3, Latch.pin20, ADC.VREF, ADC.VCC, SRAM.pin26, SRAM.pin28, GAL.pin20, GAL_NCP.1, Latch_NCP.1, ADC_NCP.2, CAN.2, Reset_CAN.Pin_0, VCC1.-, Reset_Atmega.Pin_0, JTAG_Power.pin1, SRAM_2.0
  N37: RS232.pin4, UART_connector.pin3
  N38: RS232.pin5, UART_connector.pin4
  N39: RS232.pin10, RS232.pin16
  N40: RS232.pin11, RS232.pin15
  N41: RS232.pin12, RS232.pin17
  N42: CAN_controller.pin1, CAN_trancv.pin1
  N43: CAN_controller.pin2, CAN_trancv.pin4
  N44: CAN_controller.pin7, OSC2_2.1, Clock_CAN.pin_0
  N45: CAN_controller.pin8, Clock_CAN.pin_1, OSC2_1.1
  N46: CAN_controller.pin9, OSC2_2.2, OSC2_1.2
  N47: CAN_trancv.pin6, Terminate_CAN.Pin_0, CAN_bus.pin2
  N48: CAN_trancv.pin7, Terminate_CAN.Pin_1, CAN_bus.pin1
  N49: CAN_trancv.pin8, RS_resistor.Pin_1
  N50: Latch.pin12, SRAM.pin3
  N51: Latch.pin13, SRAM.pin4
  N52: Latch.pin14, SRAM.pin5
  N53: Latch.pin15, SRAM.pin6
  N54: Latch.pin16, SRAM.pin7
  N55: Latch.pin17, SRAM.pin8
  N56: Latch.pin18, SRAM.pin9
  N57: Latch.pin19, SRAM.pin10
  N58: ADC.!CS, GAL.pin18
  N59: ADC.CH1, Game_board.pin1
  N60: ADC.CH2, Game_board.pin2
  N61: ADC.CH3, Game_board.pin3
  N62: ADC.CH4, Game_board.pin4
  N63: SRAM.pin20, GAL.pin19
  N64: GAL.pin16, Game_board.pin6
  N65: GAL.pin17, Game_board.pin5

notes:
  POWER SUPPLY, 1
  LATCH, 1
  UART - RS232, 1
  CAN BUS, 1
  GAL
  JTAG
  RESET
  UART
  STATUS ON/OFF
  GND
  5V
  CS/WR
  Data/Addr
  TX/RX
  OLED/GPIO
  Connectors, 1
  CAN
  GAME BOARD
  JTAG POW
  Noise Coupling
  Crystal Oscillator
  Voltage Regulator
  Reset Circuit

custom parts:
  DIP - 20 pins: A DIP stand-in part for whatever IC you want. With 20 pins on a 300mil dual inline package (DIP) footprint.
